// Logisim project 1bitadder.circ as structural Verilog: 1 circuit, main circuit main
module main (
  input  a1,
  input  b1,
  input  c1,
  output s1,
  output c2
);

  wire and_1_out, and_2_out, xor_1_out;

  and and_1 (and_1_out, a1, b1);
  xor xor_1 (xor_1_out, a1, b1);
  xor xor_2 (s1, xor_1_out, c1);
  and and_2 (and_2_out, xor_1_out, c1);
  or or_1 (c2, and_2_out, and_1_out);
endmodule
