// Logisim project 4-FullAdder.circ as structural Verilog: 4 circuits, main circuit 1-bit adder
module _1_bit_adder (
  input  a1,
  input  b1,
  input  c1,
  output s1,
  output c2
);

  wire and_1_out, and_2_out, xor_1_out;

  and and_1 (and_1_out, a1, b1);
  xor xor_1 (xor_1_out, a1, b1);
  xor xor_2 (s1, xor_1_out, c1);
  and and_2 (and_2_out, xor_1_out, c1);
  or or_1 (c2, and_2_out, and_1_out);
endmodule

module _4_bit_adder (
  input  C,
  input  [3:0] A,
  input  [3:0] A_2,
  output [3:0] Sum,
  output Remainder
);

  wire n1_bit_adder_1_c2, n1_bit_adder_2_c2, n1_bit_adder_3_c2;

  _1_bit_adder u_1_bit_adder_1 (.a1(A[0]), .b1(A_2[0]), .c1(C), .s1(Sum[0]), .c2(n1_bit_adder_1_c2));
  _1_bit_adder u_1_bit_adder_2 (.a1(A[1]), .b1(A_2[1]), .c1(n1_bit_adder_1_c2), .s1(Sum[1]), .c2(n1_bit_adder_2_c2));
  _1_bit_adder u_1_bit_adder_3 (.a1(A[2]), .b1(A_2[2]), .c1(n1_bit_adder_2_c2), .s1(Sum[2]), .c2(n1_bit_adder_3_c2));
  _1_bit_adder u_1_bit_adder_4 (.a1(A[3]), .b1(A_2[3]), .c1(n1_bit_adder_3_c2), .s1(Sum[3]), .c2(Remainder));
endmodule

module _8_bit_adder (
  input  a0,
  input  a1,
  input  a2,
  input  a3,
  input  a4,
  input  a5,
  input  b0,
  input  b1,
  input  b2,
  input  b3,
  input  b4,
  input  b5,
  output c6,
  output s5,
  output s4,
  output s3,
  output s2,
  output s1,
  output s0
);

  wire adder_1_cout;
  wire [3:3] adder_2_out, undriven, undriven_2;

  Adder #(.width(4)) adder_1 (
    .a({a3, a2, a1, a0}), .b({b3, b2, b1, b0}), .out({s3, s2, s1, s0}), .cin(1'b0), .cout(adder_1_cout));
  Adder #(.width(4)) adder_2 (
    .a({undriven[3], 1'b0, a5, a4}), .b({undriven_2[3], 1'b0, b5, b4}), .out({adder_2_out[3], c6, s5, s4}),
    .cin(adder_1_cout));  // open: cout
endmodule

module _8_bit_adder_Al (
  input  [3:0] a0___a3,
  input  [3:0] b0___b3,
  input  [3:0] a4___a5,
  input  [3:0] b4___b5,
  output [3:0] s0___s3,
  output [3:0] s4___s,
  output c6
);

  wire adder_1_cout;

  Adder #(.width(4)) adder_1 (.a(a0___a3), .b(b0___b3), .out(s0___s3), .cin(1'b0), .cout(adder_1_cout));
  Adder #(.width(4)) adder_2 (.a(a4___a5), .b(b4___b5), .out(s4___s), .cin(adder_1_cout), .cout(c6));
endmodule
