// Logisim project A4.circ as structural Verilog: 2 circuits, main circuit Q5
module Q5 (
  input  x,
  input  y,
  output z
);

  wire A_q, A_qn, and_1_out, and_2_out, and_3_out, and_4_out, and_5_out, and_6_out, and_7_out, B_q, B_qn,
       Clock_out, not_1_out, not_2_out, or_1_out, or_2_out;

  not not_1 (not_1_out, x);
  not not_2 (not_2_out, y);
  and and_1 (and_1_out, x, B_q);
  and and_2 (and_2_out, not_2_out, B_qn);
  and and_3 (and_3_out, x, not_2_out);
  or or_1 (or_1_out, and_1_out, and_2_out);
  and and_4 (and_4_out, B_qn, not_2_out, x);
  and and_5 (and_5_out, A_qn, x);
  or or_2 (or_2_out, A_q, and_3_out);
  Clock Clock (.out(Clock_out));
  J_K_Flip_Flop A (.J(or_1_out), .clk(Clock_out), .K(and_4_out), .Q(A_q), .Qn(A_qn));  // open: preset, en, reset
  J_K_Flip_Flop B (.J(and_5_out), .clk(Clock_out), .K(or_2_out), .Q(B_q), .Qn(B_qn));  // open: preset, en, reset
  and and_6 (and_6_out, A_q, not_1_out, not_2_out);
  and and_7 (and_7_out, not_2_out, not_1_out, B_q);
  or or_3 (z, and_6_out, and_7_out);
endmodule

module Q6 (
  input  x,
  output y
);

  wire A_q, A_qn, and_1_out, and_2_out, and_3_out, and_4_out, B_q, B_qn, Clock_out, not_1_out, or_1_out,
       or_2_out;

  not not_1 (not_1_out, x);
  and and_1 (and_1_out, A_q, not_1_out);
  and and_2 (and_2_out, x, B_qn);
  and and_3 (and_3_out, A_q, x);
  and and_4 (and_4_out, not_1_out, B_q);
  or or_1 (or_1_out, and_1_out, and_2_out);
  or or_2 (or_2_out, and_3_out, and_4_out);
  Clock Clock (.out(Clock_out));
  D_Flip_Flop A (.clk(Clock_out), .D(or_1_out), .Q(A_q), .Qn(A_qn));  // open: preset, en, reset
  D_Flip_Flop B (.clk(Clock_out), .D(or_2_out), .Q(B_q), .Qn(B_qn));  // open: preset, en, reset
  xor xor_1 (y, A_q, B_q);
endmodule
