// Logisim project Assignment 2 Q4.circ as structural Verilog: 1 circuit, main circuit main
module main (
  input  x,
  input  y,
  input  y_2,
  output F_x_y_z
);

  wire and_1_out, not_1_out, not_2_out, or_1_out;

  not not_1 (not_1_out, y_2);
  or or_1 (or_1_out, x, not_1_out);
  not not_2 (not_2_out, y);
  and and_1 (and_1_out, y, or_1_out);
  or or_2 (F_x_y_z, x, not_2_out, and_1_out);
endmodule
