// Logisim project 2F1F2.circ as structural Verilog: 1 circuit, main circuit main
module main (
  input  x,
  input  y,
  output x_xy__prime__prime__y_xy__prime__prime___prime,
  output xy__prime__xy__prime__prime
);

  wire nand_1_out, nand_2_out, nand_3_out, nand_4_out;

  nand nand_1 (nand_1_out, x, y);
  nand nand_2 (nand_2_out, x, y);
  nand nand_3 (nand_3_out, x, nand_1_out);
  nand nand_4 (nand_4_out, nand_1_out, y);
  nand nand_5 (x_xy__prime__prime__y_xy__prime__prime___prime, nand_3_out, nand_4_out);
  not nand_6 (xy__prime__xy__prime__prime, nand_2_out);  // NAND_Gate
endmodule
