// Logisim project F1F2.circ as structural Verilog: 1 circuit, main circuit main
module main (
  input  x,
  input  y,
  output x_prime_y___xy_prime,
  output xy__prime__prime
);

  wire nand_1_out, nand_2_out, nand_3_out, not_1_out, not_2_out;

  not not_1 (not_1_out, x);
  not not_2 (not_2_out, y);
  nand nand_1 (nand_1_out, not_1_out, y);
  nand nand_2 (nand_2_out, x, not_2_out);
  nand nand_3 (nand_3_out, x, y);
  nand nand_4 (x_prime_y___xy_prime, nand_1_out, nand_2_out);
  not not_3 (xy__prime__prime, nand_3_out);
endmodule
