// Logisim project Q1c.circ as structural Verilog: 1 circuit, main circuit main
module main (
  input  x,
  input  y,
  output x_prime_y_prime___xy
);

  wire and_1_out, and_2_out, not_1_out, not_2_out;

  not not_1 (not_1_out, x);
  not not_2 (not_2_out, y);
  and and_1 (and_1_out, x, y);
  and and_2 (and_2_out, not_1_out, not_2_out);
  or or_1 (x_prime_y_prime___xy, and_1_out, and_2_out);
endmodule
