// Logisim project Q2c.circ as structural Verilog: 1 circuit, main circuit main
module main (
  input  x,
  input  x_2,
  output x_prime_y_prime,
  output x_prime_y,
  output xy_prime,
  output xy
);

  wire not_1_out, not_2_out;

  not not_1 (not_1_out, x);
  not not_2 (not_2_out, x_2);
  and and_1 (x_prime_y_prime, not_1_out, not_2_out);
  and and_2 (x_prime_y, not_1_out, x_2);
  and and_3 (xy_prime, x, not_2_out);
  and and_4 (xy, x, x);
endmodule
