// Logisim project Q3c.circ as structural Verilog: 1 circuit, main circuit main
module main (
  input  x,
  input  y,
  input  z,
  output x_prime_y_prime_z_prime,
  output x_prime_y_prime_z,
  output x_prime_yz_prime,
  output x_prime_yz,
  output xy_prime_z_prime,
  output xy_prime_z,
  output xyz_prime,
  output xyz
);

  wire not_1_out, not_2_out, not_3_out;

  not not_1 (not_1_out, x);
  not not_2 (not_2_out, y);
  not not_3 (not_3_out, z);
  and and_1 (x_prime_y_prime_z_prime, not_1_out, not_2_out, not_3_out);
  and and_2 (x_prime_y_prime_z, not_1_out, not_2_out, z);
  and and_3 (x_prime_yz_prime, not_1_out, y, not_3_out);
  and and_4 (x_prime_yz, not_1_out, y, z);
  and and_5 (xy_prime_z_prime, x, not_2_out, not_3_out);
  and and_6 (xy_prime_z, x, not_2_out, z);
  and and_7 (xyz_prime, x, y, not_3_out);
  and and_8 (xyz, x, y, z);
endmodule
