// Logisim project Q1d(1).circ as structural Verilog: 1 circuit, main circuit main
module main (
  input  a1,
  input  a0,
  input  b1,
  input  b0,
  output s0,
  output s1,
  output c2
);

  wire and_1_out, and_2_out, and_3_out, xor_2_out;

  xor xor_1 (s0, a0, b0);
  and and_1 (and_1_out, a0, b0);
  xor xor_2 (xor_2_out, a1, b1);
  and and_2 (and_2_out, a1, b1);
  xor xor_3 (s1, and_1_out, xor_2_out);
  and and_3 (and_3_out, and_1_out, xor_2_out);
  or or_1 (c2, and_3_out, and_2_out);
endmodule
