// Logisim project Q1d.circ as structural Verilog: 1 circuit, main circuit main
module main (
  input  E,
  input  A,
  input  B,
  input  C,
  output X,
  output Y,
  output Z,
  output S
);

  wire and_1_out, and_2_out, and_3_out, and_4_out, and_5_out, and_6_out, not_1_out, not_2_out, not_3_out,
       not_4_out;

  not not_1 (not_1_out, E);
  not not_2 (not_2_out, A);
  not not_3 (not_3_out, B);
  not not_4 (not_4_out, C);
  and and_1 (and_1_out, not_1_out, B, not_4_out);
  and and_2 (and_2_out, not_1_out, C);
  and and_3 (and_3_out, E, B);
  and and_4 (and_4_out, not_2_out, B);
  and and_5 (and_5_out, not_1_out, not_3_out);
  and and_6 (and_6_out, E, C);
  and and_7 (S, A, A, B, C);
  or or_1 (X, A, and_1_out);
  or or_2 (Y, and_2_out, and_3_out, and_4_out);
  or or_3 (Z, and_5_out, and_6_out);
endmodule
