// Logisim project Q2.circ as structural Verilog: 2 circuits, main circuit main
module main (
  input  A,
  input  B,
  input  C,
  input  D,
  input  x,
  input  y,
  output F
);

  Multiplexer #(.select(2)) multiplexer_1 (.in0(A), .in1(B), .in2(C), .in3(D), .out(F), .sel({x, y}));  // open: en
endmodule

module _4_to_1_using_2_2_to_1 (
  input  A,
  input  B,
  input  C,
  input  D,
  input  y,
  input  in_6,
  output F
);

  wire and_1_out, and_2_out, multiplexer_1_out, multiplexer_2_out, not_1_out;

  Multiplexer multiplexer_1 (.in0(A), .in1(B), .out(multiplexer_1_out), .sel(y));  // open: en
  Multiplexer multiplexer_2 (.in0(C), .in1(D), .out(multiplexer_2_out), .sel(y));  // open: en
  not not_1 (not_1_out, in_6);
  and and_1 (and_1_out, multiplexer_1_out, not_1_out);
  and and_2 (and_2_out, multiplexer_2_out, in_6);
  or or_1 (F, and_1_out, and_2_out);
endmodule
