// Logisim project Q2a.circ as structural Verilog: 1 circuit, main circuit main
module main (
  input  a,
  input  b,
  input  A_2,
  input  B_2,
  input  C,
  input  D,
  output Q
);

  wire and_1_out, and_2_out, and_3_out, and_4_out, not_1_out, not_2_out;

  not not_1 (not_1_out, a);
  not not_2 (not_2_out, b);
  and and_1 (and_1_out, not_1_out, not_2_out, A_2);
  and and_2 (and_2_out, a, not_2_out, B_2);
  and and_3 (and_3_out, not_1_out, b, C);
  and and_4 (and_4_out, a, b, D);
  or or_1 (Q, and_1_out, and_2_out, and_3_out, and_4_out);
endmodule
