// Logisim project Q2b.circ as structural Verilog: 1 circuit, main circuit main
module main (
  input  A,
  input  B,
  input  x,
  input  C,
  input  D,
  input  y,
  output out_7
);

  wire and_1_out, and_2_out, and_3_out, and_4_out, not_1_out, not_2_out, or_1_out, or_2_out;

  and and_1 (and_1_out, A, not_1_out);
  not not_1 (not_1_out, x);
  and and_2 (and_2_out, B, x);
  and and_3 (and_3_out, C, not_2_out);
  not not_2 (not_2_out, y);
  and and_4 (and_4_out, D, y);
  or or_1 (or_1_out, and_1_out, and_2_out);
  or or_2 (or_2_out, and_3_out, and_4_out);
  or or_3 (out_7, or_1_out, or_2_out);
endmodule
