// Logisim project Q3 Main.circ as structural Verilog: 4 circuits, main circuit Q3d
module Q3d (
  input  A,
  input  B,
  input  C,
  output X
);

  wire and_1_out, and_2_out, and_3_out, not_1_out, not_2_out, not_3_out;

  not not_1 (not_1_out, A);
  not not_2 (not_2_out, C);
  not not_3 (not_3_out, B);
  and and_1 (and_1_out, not_1_out, not_3_out);
  and and_2 (and_2_out, not_1_out, not_2_out);
  and and_3 (and_3_out, A, B, C);
  or or_1 (X, and_1_out, and_2_out, and_3_out);
endmodule

module Q3e (
  input  A,
  input  B,
  input  C,
  output X
);

  wire not_1_out;

  not not_1 (not_1_out, C);
  Multiplexer #(.select(2)) multiplexer_1 (
    .in0(1'b1), .in1(1'b0), .in2(not_1_out), .in3(C), .out(X), .sel({B, A}));  // open: en
endmodule

module Q3f (
  input  A,
  input  B,
  input  C,
  output X
);

  wire and_1_out, and_2_out, multiplexer_1_out, multiplexer_2_out, not_1_out, not_2_out;

  not not_1 (not_1_out, C);
  Multiplexer multiplexer_1 (.in0(1'b1), .in1(not_1_out), .out(multiplexer_1_out), .sel(B));  // open: en
  Multiplexer multiplexer_2 (.in0(1'b0), .in1(C), .out(multiplexer_2_out), .sel(B));  // open: en
  not not_2 (not_2_out, A);
  and and_1 (and_1_out, not_2_out, multiplexer_1_out);
  and and_2 (and_2_out, multiplexer_2_out, A);
  or or_1 (X, and_1_out, and_2_out);
endmodule

module Q3f_Al (
  input  A,
  input  B,
  input  C,
  output out_4
);

  wire multiplexer_1_out, multiplexer_2_out, not_1_out;

  not not_1 (not_1_out, C);
  Multiplexer multiplexer_1 (.in0(1'b1), .in1(not_1_out), .out(multiplexer_1_out), .sel(B));  // open: en
  Multiplexer multiplexer_2 (.in0(1'b0), .in1(C), .out(multiplexer_2_out), .sel(B));  // open: en
  Multiplexer multiplexer_3 (.in0(multiplexer_1_out), .in1(multiplexer_2_out), .out(out_4), .sel(A));  // open: en
endmodule
