// Logisim project Q3d.circ as structural Verilog: 3 circuits, main circuit Q3d
module Q3d (
  input  A,
  input  B,
  input  C,
  output F
);

  wire and_1_out, and_2_out, and_3_out, and_4_out, not_1_out, not_2_out, not_3_out, not_4_out, or_1_out;

  not not_1 (not_1_out, A);
  not not_2 (not_2_out, B);
  not not_3 (not_3_out, C);
  and and_1 (and_1_out, not_1_out, not_2_out, C);
  and and_2 (and_2_out, not_1_out, B, not_3_out);
  and and_3 (and_3_out, A, not_2_out, not_3_out);
  and and_4 (and_4_out, A, B, C);
  or or_1 (or_1_out, and_1_out, and_2_out, and_3_out, and_4_out);
  not not_4 (not_4_out, or_1_out);
  and and_5 (F, not_4_out, not_1_out, not_3_out);

  // Notes on the sheet:
  //   X
endmodule

module Q3e (
  input  in_1,
  input  in_2,
  input  in_3,
  input  in_4,
  input  in_5,
  input  in_6,
  output out_7
);

  wire multiplexer_1_out, not_1_out, not_2_out;

  Multiplexer #(.select(2)) multiplexer_1 (
    .in0(in_1), .in1(in_2), .in2(in_3), .in3(in_4), .out(multiplexer_1_out), .sel({in_5, in_6}));  // open: en
  not not_1 (not_1_out, multiplexer_1_out);
  not not_2 (not_2_out, in_5);
  and and_1 (out_7, not_1_out, in_1, in_3, not_2_out);

  // Notes on the sheet:
  //   X
endmodule

module Q3f (
  input  in_1,
  input  in_2,
  input  in_3,
  input  in_4,
  input  in_5,
  input  in_6,
  output out_7
);

  wire and_1_out, and_2_out, multiplexer_1_out, multiplexer_2_out, not_1_out, not_2_out, not_3_out, or_1_out;

  Multiplexer multiplexer_1 (.in0(in_1), .in1(in_2), .out(multiplexer_1_out), .sel(in_5));  // open: en
  Multiplexer multiplexer_2 (.in0(in_3), .in1(in_4), .out(multiplexer_2_out), .sel(in_5));  // open: en
  not not_1 (not_1_out, in_6);
  and and_1 (and_1_out, multiplexer_1_out, not_1_out);
  and and_2 (and_2_out, multiplexer_2_out, in_6);
  or or_1 (or_1_out, and_1_out, and_2_out);
  not not_2 (not_2_out, or_1_out);
  not not_3 (not_3_out, in_5);
  and and_3 (out_7, not_2_out, in_1, in_3, not_3_out);
endmodule
