// Logisim project Q3.circ as structural Verilog: 3 circuits, main circuit Q3c
module Q3c (
  input  in_1,
  input  in_2,
  input  in_3,
  output out_4,
  output out_5,
  output out_6
);

  wire and_1_out, and_2_out, and_3_out, and_4_out, and_5_out, not_1_out, not_2_out;

  not not_1 (not_1_out, in_1);
  not not_2 (not_2_out, in_2);
  not not_3 (out_6, in_3);
  and and_1 (and_1_out, in_1, not_2_out);
  and and_2 (and_2_out, in_1, out_6);
  and and_3 (and_3_out, in_2, in_3);
  and and_4 (and_4_out, not_2_out, in_3);
  and and_5 (and_5_out, in_2, out_6);
  or or_1 (out_4, and_1_out, and_2_out, and_3_out);
  or or_2 (out_5, and_4_out, and_5_out);
endmodule

module Q3d (
  input  R,
  output L1,
  output L2,
  output L3
);

  wire and_1_out, clock_1_out, xor_1_out, xor_2_out;

  Clock clock_1 (.out(clock_1_out));
  D_Flip_Flop u_L1 (.clk(clock_1_out), .D(xor_1_out), .Q(L1), .en(R));  // open: Qn, preset, reset
  D_Flip_Flop u_L2 (.clk(clock_1_out), .D(xor_2_out), .Q(L2), .en(R));  // open: Qn, preset, reset
  D_Flip_Flop u_L3 (.clk(clock_1_out), .D(L3), .Qn(L3), .en(R));  // open: Q, preset, reset
  xor xor_1 (xor_1_out, L1, and_1_out);
  xor xor_2 (xor_2_out, L2, L3);
  and and_1 (and_1_out, L3, L2);
endmodule

module Q4 (
  input  D,
  output Q
);

  wire Clock_out, nand_1_out, nand_2_out, nand_3_out, nand_4_out, nand_5_out, nand_6_out, nand_8_out,
       not_1_out, not_2_out, not_3_out;

  Clock Clock (.out(Clock_out));
  not not_1 (not_1_out, D);
  not not_2 (not_2_out, Clock_out);
  nand nand_1 (nand_1_out, D, not_2_out);
  nand nand_2 (nand_2_out, not_2_out, not_1_out);
  nand nand_3 (nand_3_out, nand_1_out, nand_4_out);
  nand nand_4 (nand_4_out, nand_3_out, nand_2_out);
  not not_3 (not_3_out, nand_3_out);
  nand nand_5 (nand_5_out, nand_3_out, Clock_out);
  nand nand_6 (nand_6_out, Clock_out, not_3_out);
  nand nand_7 (Q, nand_5_out, nand_8_out);
  nand nand_8 (nand_8_out, Q, nand_6_out);
endmodule
