// Logisim project Q12.circ as structural Verilog: 2 circuits, main circuit Q1
module Q1 (
  input  X,
  output Y,
  output Z
);

  wire and_1_out, and_2_out, and_3_out, clock_1_out, d_ff_1_qn, d_ff_2_qn, not_1_out, or_1_out, xor_1_out;

  not not_1 (not_1_out, X);
  and and_1 (and_1_out, Y, X);
  and and_2 (and_2_out, not_1_out, d_ff_1_qn);
  and and_3 (and_3_out, X, d_ff_2_qn);
  xor xor_1 (xor_1_out, and_1_out, Z);
  or or_1 (or_1_out, and_2_out, and_3_out);
  Clock clock_1 (.out(clock_1_out));
  D_Flip_Flop d_ff_1 (.clk(clock_1_out), .D(xor_1_out), .Q(Y), .Qn(d_ff_1_qn));  // open: preset, en, reset
  D_Flip_Flop d_ff_2 (.clk(clock_1_out), .D(or_1_out), .Q(Z), .Qn(d_ff_2_qn));  // open: preset, en, reset
endmodule

module Q3 (
  output out_1,
  output out_2,
  output out_3,
  output out_4,
  output out_5,
  output out_6,
  output out_7,
  output out_8
);

  wire clock_1_out, d_ff_1_q, d_ff_1_qn, undriven;

  Clock clock_1 (.out(clock_1_out));
  D_Flip_Flop d_ff_1 (.clk(clock_1_out), .D(d_ff_1_qn), .Q(d_ff_1_q), .Qn(d_ff_1_qn));  // open: preset, en, reset
  Shift_Register shift_register_1 (
    .in(d_ff_1_q), .clk(clock_1_out), .q0(out_1), .d1(undriven), .q1(out_2), .d2(undriven), .q2(out_3),
    .q3(out_4), .q4(out_5), .q5(out_6), .q6(out_7), .q7(out_8));  // open: shift, out, load, clr, d0, d3, d4, d5, d6, d7
endmodule
